# Fritzing sketch APS_Pot Sketch (saved by Fritzing 0.9.3b)
breadboards: 1

parts:
  Part1 = Arduino Uno (Rev3)
  U4 = POT [package=alps_pot]

nets:
  N1: Part1.A0, U4.S
  N2: Part1.GND, U4.E
  N3: Part1.5V, U4.A
